# Fritzing sketch watchdog (saved by Fritzing 0.9.10b)
breadboards: 2

parts:
  Bauteil1 = Arduino Mega ADK (Rev3)
  Bauteil2 = Logic Level Converter
  A1 = Werner Rothschopf (modified to ESP32-S3-DevKitC dual USB by vanepp Aug 2024)

nets:
  N1: Bauteil1.D19/RX1, Bauteil2.TX2_HV
  N2: Bauteil1.D18/TX1, Bauteil2.RX2_HV
  N3: Bauteil1.5V, Bauteil2.HV
  N4: Bauteil2.TX2_LV, A1.Pin_9
  N5: Bauteil2.RX2_LV, A1.Pin_8
  N6: Bauteil2.LV, A1.Pin_1, A1.Pin_2
  N7: A1.Pin_22, A1.Pin_23, A1.Pin_24, A1.Pin_44

custom parts:
  Werner Rothschopf (modified to ESP32-S3-DevKitC dual USB by vanepp Aug 2024): ESP32-S3 ESP32-S3-DevKitC-1 Dual USB development board Pyboard CircuitPython Micropython wifi BLE5.0 ESP32-S3.
